# Fritzing sketch iotScheme (saved by Fritzing 0.9.3b)
breadboards: 1

parts:
  U1 = NodeMCU V1.0
  Componente1 = Adafruit_BMP280
  DHT1 = DHT22 Humidity and Temperature Sensor

nets:
  N1: U1.D1, Componente1.SCK/SCL
  N2: U1.D2, Componente1.SDI/SDA
  3V3: U1.3V3, Componente1.VIN, DHT1.VDD
  GND: U1.GND, Componente1.GND, DHT1.GND
  N3: U1.D5, DHT1.DATA

custom parts:
  NodeMCU V1.0: ESP8266 based NodeMCU
  Adafruit_BMP280: Bosch has stepped up their game with their new BMP280 sensor, an environmental sensor with temperature, barometric pressure that is the next generation upgrade to the BMP085/BMP180/BMP183. This sensor is great for all sorts of weather sensing and can even be used in both I2C and SPI! This precision sensor from Bosch is the best low-cost, precision sensing solution for measuring barometric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
